# Fritzing sketch SISTEMA DE RIEGO INTELIGENTE (saved by Fritzing 0.9.3b)
breadboards: 1

parts:
  U1 = L9110 H-bridge module [part_number="L9110 H-bridge"]
  Componente2 = Arduino Uno (Rev3)
  Componente3 = FC-28 Soil Hygrometer Module - Probe
  M1 = DC Motor
  Water_Level_Sensor1 = Water Level Sensor
  LED1 = LED - 5mm [color="Yellow (595nm)" package="5 mm [THT]"]
  LED2 = LED - 5mm [color="Green (570nm)" package="5 mm [THT]"]
  LED3 = LED - 5mm [color="Red (633nm)" package="5 mm [THT]"]
  LED4 = LED - 5mm [color="Orange (620nm)" package="5 mm [THT]"]
  Componente4 = FC-28 Soil Hygrometer Module

nets:
  N1: U1.B-IA, Componente2.D10_PWM/SS
  N2: U1.B-IB, Componente2.D11_PWM/MOSI
  N3: U1.MOTOR_B-A, M1.pin_2
  N4: U1.MOTOR_B-B, M1.pin_1
  N5: Componente2.A0, Water_Level_Sensor1.SIG
  N6: Componente2.A1, Componente4.AO
  N7: Componente2.D8, LED4.anode
  N8: Componente2.D9_PWM, LED3.anode
  N9: Componente2.D12/MISO, LED2.anode
  N10: Componente2.D13/SCK, LED1.anode
  GND: Componente2.GND, Water_Level_Sensor1.GND, LED1.cathode, LED2.cathode, LED3.cathode, LED4.cathode, Componente4.GND
  VCC: Componente2.5V, Water_Level_Sensor1.VCC, Componente4.VCC
  N11: Componente3.POS, Componente4.POS
  N12: Componente3.NEG, Componente4.NEG

custom parts:
  FC-28 Soil Hygrometer Module - Probe: The FC-28 is a soil hygrometer module that uses the Texas Instruments LM393 comparator chip to provide an analog measurement of soil humidity.
  Water Level Sensor: A water level sensor. This sensor operates at 3V to 5V. The Sig (signal) pin outputs an analogue signal that is in proportion to the amount of water in contact with the sensor.
  FC-28 Soil Hygrometer Module: The FC-28 is a soil hygrometer module that uses the Texas Instruments LM393 comparator chip to provide an analog measurement of soil humidity. The digital output is high when soil moisture is over a certain threshold, as determined by adjusting the potentiometer.
