# Fritzing sketch Carrito (saved by Fritzing 0.9.3b)
breadboards: 1

parts:
  M1 = DC Motor
  M2 = DC Motor
  Componente1 = Arduino Uno (Rev3)
  Componente2 = HC-SR04
  Componente3 = Module Bluetooth
  U1 = L9110 H-bridge module [part_number="L9110 H-bridge"]
  U2 = SWITCH-SPST-2 [package=switch-spst-vertical]
  VCC1 = Battery block 9V

nets:
  N1: M1.pin_1, U1.MOTOR_A-B
  N2: M1.pin_2, U1.MOTOR_A-A
  N3: M2.pin_1, U1.MOTOR_B-B
  N4: M2.pin_2, U1.MOTOR_B-A
  N5: Componente1.D8, Componente2.Echo
  N6: Componente1.D9_PWM, Componente2.Trig
  N7: Componente1.D10_PWM/SS, U1.A-IB
  N8: Componente1.D11_PWM/MOSI, U1.A-IA
  N9: Componente1.D12/MISO, U1.B-IB
  N10: Componente1.D13/SCK, U1.B-IA
  N11: Componente1.D0/RX, Componente3.RXD
  N12: Componente1.D1/TX, Componente3.TXD
  VCC: Componente1.5V, Componente2.Vcc, Componente3.VCC, U1.VCC, U2.P, VCC1.+
  GND: Componente1.GND, Componente2.Gnd, Componente3.GND, U1.GND
  N13: U2.O, VCC1.-

custom parts:
  HC-SR04: HC-SR04 ultrasonic distance sensor
