# Fritzing sketch leds_sonidoFZ (saved by Fritzing 0.9.3b)
breadboards: 1

parts:
  Componente1 = Arduino Uno (Rev3)
  Mic1 = KY-038
  LED1 = smd LED [color="Green (570nm)" package="0603 [SMD]"]
  LED2 = smd LED [color="Yellow (595nm)" package="0603 [SMD]"]
  LED3 = smd LED [color="Orange (605nm)" package="0603 [SMD]"]
  LED4 = smd LED [color="Red (633nm)" package="0603 [SMD]"]

nets:
  N1: Componente1.A0, Componente1.GND, Mic1.pin1, Mic1.pin2, LED1.cathode, LED2.cathode, LED3.cathode
  N2: Componente1.D10_PWM/SS, LED3.anode
  N3: Componente1.D11_PWM/MOSI, LED4.anode
  N4: Componente1.D12/MISO, LED1.anode
  N5: Componente1.D13/SCK, LED2.anode
  N6: Componente1.5V, Mic1.pin3

custom parts:
  KY-038: ky-038 Microphone sound sensor module
