# Fritzing sketch motor1 (saved by Fritzing 0.9.3b)
breadboards: 1

parts:
  U1 = L9110 H-bridge module [part_number="L9110 H-bridge"]
  Componente2 = Arduino Uno (Rev3)
  Componente3 = FC-28 Soil Hygrometer Module - Probe  # not connected
  M1 = DC Motor
  Water_Level_Sensor1 = Water Level Sensor  # not connected
  M2 = DC Motor
  BAT1 = BC9VPC [package=bc9vpc]

nets:
  N1: U1.B-IA, Componente2.D11_PWM/MOSI
  N2: U1.B-IB, Componente2.D10_PWM/SS
  GND: U1.GND, Componente2.GND, BAT1.V-
  VCC: U1.VCC, Componente2.VIN, BAT1.V+
  N3: U1.A-IA, Componente2.D6_PWM
  N4: U1.A-IB, Componente2.D5_PWM
  N5: U1.MOTOR_A-A, M2.pin_2
  N6: U1.MOTOR_A-B, M2.pin_1
  N7: U1.MOTOR_B-A, M1.pin_2
  N8: U1.MOTOR_B-B, M1.pin_1

custom parts:
  FC-28 Soil Hygrometer Module - Probe: The FC-28 is a soil hygrometer module that uses the Texas Instruments LM393 comparator chip to provide an analog measurement of soil humidity.
  Water Level Sensor: A water level sensor. This sensor operates at 3V to 5V. The Sig (signal) pin outputs an analogue signal that is in proportion to the amount of water in contact with the sensor.
